# Fritzing sketch FSR (saved by Fritzing 0.9.3b)
circuit board: 8.46667cm x 5.64444cm
breadboards: 1

parts:
  Part2 = Arduino Uno (Rev3) - ICSP
  J1 = Basic Force Sensing Resistor (FSR) [package=THT]
  R1 = Resistor [tolerance=±5% resistance=220 package="0603 [SMD]"]

nets:
  N1: Part2.A0, J1.pin_1, R1.Pin_1
  N2: Part2.GND, R1.Pin_0
  N3: Part2.5V, J1.pin_0
